# Fritzing sketch arpcube-final (saved by Fritzing 0.8.7b)
breadboards: 3

parts:
  Part2 = Arduino Uno (Rev3)
  DIN1 = DIN-5 jack (MIDI) [package=THT]
  TRELLIS1 = Adafruit Trellis
  TRELLIS2 = Adafruit Trellis  # not connected
  R1 = Resistor [tolerance=±5% resistance=220 package=THT]
  U5 = POT [package=alps_pot]
  U6 = POT [package=alps_pot]
  U7 = POT [package=alps_pot]
  C1 = Capacitor [package=cap-pth-small2]
  S1 = Pushbutton [package="[THT]"]
  S2 = Pushbutton [package="[THT]"]
  R3 = Resistor [tolerance=±5% resistance=220 package=THT]
  R4 = Resistor [tolerance=±5% resistance=220 package=THT]
  U8 = LCD-16X2 [package=lcd-16x2]
  R2 = Resistor [tolerance=±5% resistance=220 package=THT]

nets:
  N1: Part2.A0, U7.S
  N2: Part2.A1, U5.S, U5.A, C1.2
  N3: Part2.A2, U6.S
  N4: Part2.A4/SDA, TRELLIS1.SDA
  N5: Part2.A5/SCL, TRELLIS1.SCL
  N6: Part2.D8, U8.DB4
  N7: Part2.D9_PWM, U8.DB5
  N8: Part2.D10_PWM/SS, U8.DB6
  N9: Part2.D11_PWM/MOSI, U8.DB7
  N10: Part2.D12/MISO, U8.E
  N11: Part2.D13/SCK, U8.RS
  GND: Part2.GND, DIN1.2, TRELLIS1.GND, U6.A, U7.A, C1.1, R3.Pin_0, R4.Pin_1, U8.VSS, U8.R_W, U8.K
  N12: Part2.D1/TX, R1.Pin_1
  N13: Part2.D2, TRELLIS1.INT
  N14: Part2.D5_PWM, U8.VO
  N15: Part2.D6_PWM, S1.Pin_1, S1.Pin_2, R4.Pin_0
  N16: Part2.D7, S2.Pin_1, S2.Pin_2, R3.Pin_1
  5V: Part2.5V, TRELLIS1.5V, U5.E, U6.E, U7.E, S2.Pin_3, S2.Pin_4, U8.VDD, U8.A, R2.Pin_1
  N17: DIN1.4, R1.Pin_0
