# Fritzing sketch arpcube (saved by Fritzing 0.8.7b)
breadboards: 2

parts:
  Part1 = Arduino Uno (Rev3)
  Part2 = Arduino Uno (Rev3)
  U1 = BUTTONPAD-4X4 [package=buttonpad-4x4]  # not connected
  U2 = BUTTONPAD-4X4 [package=buttonpad-4x4]
  S1 = SPST Switch [package=switch-spdt_lock.007s]
  S2 = SPST Switch [package=switch-spdt_lock.007s]
  R1 = Resistor [tolerance=±5% resistance=220 package=THT]
  R2 = TRIMPOT [package=trimpot-3mm]
  R3 = TRIMPOT [package=trimpot-3mm]
  R4 = TRIMPOT [package=trimpot-3mm]
  R5 = Resistor [tolerance=±5% resistance=220 package=THT]  # not connected
  C1 = Capacitor [package=cap-pth-small2]
  DIN1 = DIN-5 jack (MIDI) [package=THT]
  R6 = Resistor [tolerance=±5% resistance=220 package=THT]
  Part3 = DeuLigne 1.1 - The Snootlab's LCD shield for Arduino
  U4 = Bluetooth SMD Module [package=blueradio_br-c40a]
  U5 = Bluetooth SMD Module [package=blueradio_br-c40a]

nets:
  N1: Part1.A0, R2.CW, R3.CW
  N2: Part1.A1, R4.CW
  N3: Part1.D12/MISO, S2.S
  N4: Part1.AREF, S1.S
  N5: Part1.D5_PWM, U4.SPI_MISO
  N6: Part1.D6_PWM, U4.PIO_2_CONNECT
  N7: Part2.A3, U5.SPI_CLK
  N8: Part2.D8, U5.SPI_CSB
  N9: Part2.D10_PWM/SS, U5.PCM_OUT
  N10: Part2.D12/MISO, U5.GND
  N11: Part2.GND, U2.G$13_GRN, Part3.AREF, Part3.D3
  N12: Part2.D0/RX, Part3.D0_RX
  N13: Part2.D2, Part3.D1_TX, Part3.D2
  N14: Part2.D3_PWM, Part3.D5
  N15: Part2.D4, Part3.D6
  N16: Part2.D5_PWM, Part3.D12_MISO
  N17: Part2.D6_PWM, Part3.D13_SCK
  N18: Part2.D7, Part3.GND
  N19: Part2.5V, U2.G$15_BLU
  N20: Part2.VIN, Part3.D9
  N21: S1.O, R1.Pin_0
  N22: R4.CCW, C1.1
  N23: DIN1.GND, R6.Pin_0
